# Fritzing sketch uhppoted-wiegand-pico-emulator (saved by Fritzing 0.9.10b)
breadboards: 4

parts:
  M1 = RioRand LM2596
  Part1 = Adafruit 4-channel I2C-safe Bi-directional Logic Level Converter [part_number="Adafruit #757"]
  LED3 = LED - 3mm [color="Orange (620nm)" current=0.030 package="3 mm [THT]"]
  LED4 = LED - 3mm [color="Red (633nm)" current=0.030 package="3 mm [THT]"]
  LED1 = LED - 3mm [color="Green (555nm)" current=0.030 package="3 mm [THT]"]
  R4 = Resistor [tolerance=±5% resistance=1k package="0402 [SMD]"]
  LED2 = LED - 3mm [color="Yellow (585nm)" current=0.030 package="3 mm [THT]"]
  BZR1 = Piezo Speaker
  J4 = female pin header, 2 pins [form="♀ (female)"]
  R5 = Resistor [tolerance=±5% resistance=1k package="0402 [SMD]"]
  12VDC = Camdenboss CTB0158-2 [part_number=CTB0158-2 package=THT]
  Wiegand_reader_(emulation) = Camdenboss CTB0158-5 [part_number=CTB0158-5 package=THT]
  R6 = Resistor [tolerance=±5% power=0.25 resistance=1k package=THT]
  Door_lock_relay = Camdenboss CTB0158-3 [part_number=CTB0158-3 package=THT]
  Part3 = TXB0104 4-channel Bi-Directional Level Shifter
  R12 = Resistor [tolerance=±5% power=0.25 resistance=10k package=THT]
  R13 = Resistor [tolerance=±5% power=0.25 resistance=10k package=THT]
  Part4 = Adafruit 4-channel I2C-safe Bi-directional Logic Level Converter [part_number="Adafruit #757"]
  R7 = Resistor [tolerance=±5% power=0.25 resistance=1k package=THT]
  R2 = Resistor [tolerance=±5% resistance=1k power=0.25 package=THT]
  R1 = Resistor [tolerance=±5% resistance=1k power=0.25 package=THT]
  R3 = Resistor [tolerance=±5% resistance=1k power=0.25 package=THT]
  Mod1 = Raspberry Pi Pico
  IC3 = DIP - 20 pins [chip_label=TPIC6B595 package="DIP (Dual Inline) [THT]"]
  IC4 = IC, DIP package, 14 pins [chip_label=HE722A0510]
  IC5 = IC, DIP package, 14 pins [chip_label=HE722A0510]
  Door_contact_(emulation) = Camdenboss CTB0158-2 [part_number=CTB0158-2 package=THT]
  Pushbutton_(emulation) = Camdenboss CTB0158-2 [part_number=CTB0158-2 package=THT]

nets:
  12V: M1.Pin_1, 12VDC.pin1, Wiegand_reader_(emulation).pin1
  GND: M1.Pin_2, M1.Pin_4, Part1.GND, 12VDC.pin2, Wiegand_reader_(emulation).pin2, Door_lock_relay.pin1, Part3.GND, Part4.GND, Mod1.pin_3, Mod1.pin_8, Mod1.pin_11, Mod1.pin_13, Mod1.pin_18, Mod1.pin_23, Mod1.pin_28, Mod1.pin_33, Mod1.pin_38, IC3.pin9, IC3.pin10, IC3.pin11, IC3.pin19, IC4.pin7, IC5.pin7
  5V: M1.Pin_3, Part1.HV, R4.Pin_1, R6.Pin_0, Part3.HV, R12.Pin_1, R13.Pin_1, Part4.HV, R7.Pin_0, R2.Pin_1, R1.Pin_1, R3.Pin_1, Mod1.pin_39, IC3.pin2, IC3.pin8, IC4.pin2, IC5.pin2
  N1: Part1.A4, Mod1.pin_29, Mod1.pin_31
  N2: Part1.A3, Mod1.pin_26, Mod1.pin_32
  N3: Part1.A2, Mod1.pin_27, Mod1.pin_34
  3.3V: Part1.LV, BZR1.pin2, Part3.OE, Part3.LV, Part4.LV, Mod1.pin_36
  N4: Part1.B4, Wiegand_reader_(emulation).pin5
  N5: Part1.B3, Wiegand_reader_(emulation).pin4
  N6: Part1.B2, Wiegand_reader_(emulation).pin3
  N7: LED3.cathode, IC3.pin15
  N8: LED3.anode, R3.Pin_0
  N9: LED4.cathode, IC3.pin14
  N10: LED4.anode, R4.Pin_0
  N11: LED1.cathode, IC3.pin17
  N12: LED1.anode, R1.Pin_0
  N13: LED2.cathode, IC3.pin16
  N14: LED2.anode, R2.Pin_0
  N15: BZR1.pin1, R5.Pin_0
  N16: J4.pin1, Mod1.pin_2
  N17: J4.pin2, Mod1.pin_1
  N18: R5.Pin_1, Mod1.pin_12
  N19: R6.Pin_1, Door_lock_relay.pin3, Part4.B2
  N20: Door_lock_relay.pin2, Part4.B1, R7.Pin_1
  N21: Part3.B1, IC3.pin13
  N22: Part3.B2, IC3.pin3
  N23: Part3.B4, IC3.pin12
  N24: Part3.A4, Mod1.pin_17
  N25: Part3.A2, Mod1.pin_15
  N26: Part3.A1, Mod1.pin_14
  N27: R12.Pin_0, Part4.B3, IC4.pin1
  N28: R13.Pin_0, Part4.B4, IC5.pin1
  N29: Part4.A4, Mod1.pin_20
  N30: Part4.A3, Mod1.pin_19
  N31: Part4.A2, Mod1.pin_21
  N32: Part4.A1, Mod1.pin_22
  N33: IC3.pin5, IC5.pin6
  N34: IC3.pin6, IC4.pin6
  N35: IC4.pin8, Door_contact_(emulation).pin2
  N36: IC4.pin14, Door_contact_(emulation).pin1
  N37: IC5.pin8, Pushbutton_(emulation).pin2
  N38: IC5.pin14, Pushbutton_(emulation).pin1

custom parts:
  Adafruit 4-channel I2C-safe Bi-directional Logic Level Converter: Because the Arduino (and Basic Stamp) are 5V devices, and most modern sensors, displays, flash cards and modes are 3.3V-only, many makers find that they need to perform level shifting/conversion to protect the 3.3V device from 5V. We do have some other handy level shifters in the shop, from the DIP 74LVC245 to the fancy bi-directional TXB0108. However, neither of these are happy to work with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
  TXB0104 4-channel Bi-Directional Level Shifter: Because the Arduino (and Basic Stamp) are 5V devices, and most modern sensors, displays, flash cards and modes are 3.3V-only, many makers find that they need to perform level shifting/conversion to protect the 3.3V device from 5V. Although one can use resistors to make a divider, for high speed transfers, the resistors can add a lot of slew and cause havoc that is tough to debug. For that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
  Raspberry Pi Pico: Raspberry Pi Pico. Based around the RP2040 microcontroller the Pico is a low cost microcontroller device bringing Raspberry Pi quality, cost, and easy of use to the microcontroller space. Jan 2021, Split part in to two versions: tht (this one) and SMD. This one will drill holes for a .1 in header in pcb to allow plugging in the module as well as providing pads to solder the module to the top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
  DIP - 20 pins: A DIP stand-in part for whatever IC you want. With 20 pins on a 300mil dual inline package (DIP) footprint.
