# Fritzing sketch uhppoted-wiegand-pico (saved by Fritzing 0.9.10b)
breadboards: 4

parts:
  M1 = RioRand LM2596
  Part1 = Adafruit 4-channel I2C-safe Bi-directional Logic Level Converter [part_number="Adafruit #757"]
  LED3 = LED - 3mm [color="Orange (620nm)" current=0.030 package="3 mm [THT]"]
  LED4 = LED - 3mm [color="Red (633nm)" current=0.030 package="3 mm [THT]"]
  LED1 = LED - 3mm [color="Green (555nm)" current=0.030 package="3 mm [THT]"]
  R1 = Resistor [tolerance=±5% resistance=1k package="0402 [SMD]"]
  R3 = Resistor [tolerance=±5% resistance=1k package="0402 [SMD]"]
  R4 = Resistor [tolerance=±5% resistance=1k package="0402 [SMD]"]
  LED2 = LED - 3mm [color="Yellow (585nm)" current=0.030 package="3 mm [THT]"]
  BZR1 = Piezo Speaker
  J4 = female pin header, 2 pins [form="♀ (female)"]
  J5 = female pin header, 3 pins [form="♀ (female)"]
  Mod1 = Raspberry Pi Pico
  Part2 = Adafruit SDIO microSD Breakout
  R2 = Resistor [tolerance=±5% resistance=1k package="0402 [SMD]"]
  R5 = Resistor [tolerance=±5% resistance=1k package="0402 [SMD]"]
  J6 = Camdenboss CTB0158-2 [part_number=CTB0158-2 package=THT]
  J7 = Camdenboss CTB0158-5 [part_number=CTB0158-5 package=THT]
  R7 = Resistor [tolerance=±5% power=0.25 resistance=1k package=THT]
  R6 = Resistor [tolerance=±5% power=0.25 resistance=1k package=THT]
  R8 = Resistor [tolerance=±5% power=0.25 resistance=10k package=THT]
  R9 = Resistor [tolerance=±5% power=0.25 resistance=10k package=THT]
  J9 = Camdenboss CTB0158-2 [part_number=CTB0158-2 package=THT]
  Mod2 = KY-019 5V Relay Module [package="Breakout board"]
  DPDT_Relay1 = DPDT Relay [chip_label=Relay package="DIP (Dual Inline) [THT]"]
  DPDT_Relay2 = DPDT Relay [chip_label=Relay package="DIP (Dual Inline) [THT]"]
  J10 = Camdenboss CTB0158-2 [part_number=CTB0158-2 package=THT]
  J8 = Camdenboss CTB0158-3 [part_number=CTB0158-3 package=THT]
  TPIC6596 = IC, DIP package, 20 pins [chip_label=TPIC6596]

nets:
  N1: M1.Pin_1, J6.pin1, J7.pin1
  GND: M1.Pin_2, M1.Pin_4, Part1.GND, J5.pin2, Mod1.pin_3, Mod1.pin_8, Mod1.pin_11, Mod1.pin_13, Mod1.pin_18, Mod1.pin_23, Mod1.pin_28, Mod1.pin_33, Mod1.pin_38, Mod1.pin_42, Part2.GND, J6.pin2, J7.pin2, Mod2.-, J8.pin1, TPIC6596.pin1, TPIC6596.pin10, TPIC6596.pin11, TPIC6596.pin20
  5V: M1.Pin_3, Part1.HV, Mod1.pin_39, Mod2.+, DPDT_Relay1.pin8, DPDT_Relay2.pin8, TPIC6596.pin2
  N2: Part1.A4, Mod1.pin_26, Mod1.pin_27
  N3: Part1.A3, Mod1.pin_21, Mod1.pin_24
  N4: Part1.A2, Mod1.pin_22, Mod1.pin_25
  3.3V: Part1.LV, R1.Pin_0, R3.Pin_0, R4.Pin_0, BZR1.pin2, Mod1.pin_36, Part2.3.3V, R2.Pin_0, R7.Pin_0, R6.Pin_0
  N5: Part1.B4, J7.pin5
  N6: Part1.B3, J7.pin4
  N7: Part1.B2, J7.pin3
  N8: LED3.cathode, Mod1.pin_17
  N9: LED3.anode, R3.Pin_1
  N10: LED4.cathode, Mod1.pin_15
  N11: LED4.anode, R4.Pin_1
  N12: LED1.cathode, Mod1.pin_20
  N13: LED1.anode, R1.Pin_1
  N14: LED2.cathode, Mod1.pin_19
  N15: LED2.anode, R2.Pin_1
  N16: BZR1.pin1, R5.Pin_0
  N17: J4.pin1, Mod1.pin_2
  N18: J4.pin2, Mod1.pin_1
  N19: J5.pin1, Mod1.pin_43
  N20: J5.pin3, Mod1.pin_41
  N21: Mod1.pin_4, Part2.SCLK
  N22: Mod1.pin_5, Part2.DI
  N23: Mod1.pin_6, Part2.DO
  N24: Mod1.pin_7, Part2.CS
  N25: Mod1.pin_9, Part2.CARDDET
  N26: Mod1.pin_16, R5.Pin_1
  N27: Mod1.pin_32, R9.Pin_1
  N28: Mod1.pin_34, R8.Pin_1
  N29: R7.Pin_1, R9.Pin_0, J8.pin3
  N30: R6.Pin_1, R8.Pin_0, J8.pin2
  N31: J9.pin1, DPDT_Relay1.pin7
  N32: J9.pin2, DPDT_Relay1.pin5
  N33: Mod2.S, TPIC6596.pin7
  N34: DPDT_Relay1.pin1, TPIC6596.pin17
  N35: DPDT_Relay2.pin1, TPIC6596.pin16
  N36: DPDT_Relay2.pin5, J10.pin2
  N37: DPDT_Relay2.pin7, J10.pin1

custom parts:
  Adafruit 4-channel I2C-safe Bi-directional Logic Level Converter: Because the Arduino (and Basic Stamp) are 5V devices, and most modern sensors, displays, flash cards and modes are 3.3V-only, many makers find that they need to perform level shifting/conversion to protect the 3.3V device from 5V. We do have some other handy level shifters in the shop, from the DIP 74LVC245 to the fancy bi-directional TXB0108. However, neither of these are happy to work with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
  Raspberry Pi Pico: Raspberry Pi Pico. Based around the RP2040 microcontroller the Pico is a low cost microcontroller device bringing Raspberry Pi quality, cost, and easy of use to the microcontroller space. Jan 2021, Split part in to two versions: tht (this one) and SMD. This one will drill holes for a .1 in header in pcb to allow plugging in the module as well as providing pads to solder the module to the top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
  KY-019 5V Relay Module: KY-019 5V Relay module, used to control AC circuits. (Special thanks to vanepp for fixing the PCB holes and other errors)
  DPDT Relay: DIP DPDT Relay (Double Pole Double Throw)
